// Logisim project single_circle.circ as structural Verilog: 8 circuits, main circuit main
module main (
  input  Reset,
  output [31:0] out_2,
  output out_3,
  output [4:0] out_4,
  output [31:0] out_5,
  output out_6,
  output [4:0] out_7,
  output [31:0] out_8
);

  wire ALU_zero, and_1_out, bitfinder_1_found, clock_1_out, comparator_1_lt, controller_1_branch,
       controller_1_jump, isImm, not_1_out, not_2_out;
  wire [1:0] controller_1_extop, controller_1_regdst, controller_1_regsrc;
  wire [1:1] controller_1_alusrc;
  wire [3:0] _31_28, controller_1_aluctrl;
  wire [4:0] bit_extender_1_out;
  wire [9:0] bit_extender_3_out, shifter_3_out;
  wire [27:0] adder_2_out;
  wire [31:0] adder_1_out, adder_3_out, ALU_result, bit_extender_2_out, ext_1_immout, jumpto,
       multiplexer_1_out, multiplexer_2_out, multiplexer_3_out, multiplexer_6_out, multiplexer_7_out, PC_q,
       ram_1_data, RData1, shifter_1_out, shifter_2_out;

  Multiplexer #(.width(32)) multiplexer_1 (
    .in0({_31_28, adder_2_out}), .in1(adder_3_out), .out(multiplexer_1_out), .sel(and_1_out));  // open: en
  Clock clock_1 (.out(clock_1_out));
  Multiplexer #(.width(32)) multiplexer_2 (
    .in0(multiplexer_1_out), .in1(jumpto), .out(multiplexer_2_out), .sel(controller_1_jump));  // open: en
  Register #(.width(32)) PC (.D(multiplexer_2_out), .Q(PC_q), .clk(clock_1_out), .clr(Reset));  // open: en
  Multiplexer #(.width(32)) multiplexer_3 (
    .in0(PC_q), .in1(adder_1_out), .out(multiplexer_3_out), .sel(comparator_1_lt));  // open: en
  Adder #(.width(32)) adder_1 (.a(PC_q), .b(32'h3000), .out(adder_1_out));  // open: cin, cout
  Comparator #(.width(32)) comparator_1 (.a(PC_q), .b(32'h3000), .lt(comparator_1_lt));  // open: gt, eq
  Bit_Extender #(.in_width(32), .out_width(5)) bit_extender_1 (.in(shifter_1_out), .out(bit_extender_1_out));
  Shifter #(.width(32), .shift("lr")) shifter_1 (.in(multiplexer_3_out), .\dist (5'b00010), .out(shifter_1_out));
  Adder #(.width(32)) adder_2 (.a(multiplexer_3_out), .b(32'h4), .out({_31_28, adder_2_out}));  // open: cin, cout
  Multiplexer #(.width(32)) multiplexer_4 (
    .in0(RData1), .in1({_31_28, out_2[25:0], 2'b00}), .out(jumpto), .sel(isImm));  // open: en
  ROM #(.addrWidth(5), .dataWidth(32)) rom_1 (.addr(bit_extender_1_out), .data(out_2));  // open: sel
  not not_1 (not_1_out, bitfinder_1_found);
  BitFinder #(.width(32), .\type ("high1")) bitfinder_1 (.in(out_2), .found(bitfinder_1_found));  // open: index
  Controller controller_1 (
    .Op(out_2[31:26]), .funct(out_2[5:0]), .jump(controller_1_jump), .ExtOp(controller_1_extop),
    .RegSrc(controller_1_regsrc), .MemWrite(out_6), .Branch(controller_1_branch),
    .ALUCtrl(controller_1_aluctrl), .RegDst(controller_1_regdst), .RegWrite(out_3), .RT(out_2[20:16]),
    .ALUSrc({controller_1_alusrc[1], isImm}), .in_4(not_1_out));
  // Probe on controller_1_aluctrl
  ext ext_1 (.ExtOp(controller_1_extop), .Imm(out_2[15:0]), .Immout(ext_1_immout));
  register_file Register_File (
    .WEnable(out_3), .clock(clock_1_out), .reset(Reset), .RAddress1(out_2[25:21]), .RAddress2(out_2[20:16]),
    .WAddress(out_4), .WData(out_5), .RData1(RData1), .RData2(out_8));
  Multiplexer #(.select(2), .width(5)) multiplexer_5 (
    .in0(out_2[20:16]), .in1(out_2[15:11]), .in2({5{1'b1}}), .out(out_4), .sel(controller_1_regdst));  // open: in3, en
  assign bit_extender_2_out = {{27{1'b0}}, out_2[10:6]};  // Bit_Extender bit_extender_2
  Adder #(.width(32)) adder_3 (.a(ext_1_immout), .b({_31_28, adder_2_out}), .out(adder_3_out));  // open: cin, cout
  Multiplexer #(.width(32)) multiplexer_6 (
    .in0(RData1), .in1(bit_extender_2_out), .out(multiplexer_6_out), .sel(controller_1_alusrc[1]));  // open: en
  Multiplexer #(.width(32)) multiplexer_7 (
    .in0(out_8), .in1(ext_1_immout), .out(multiplexer_7_out), .sel(isImm));  // open: en
  ALU ALU (
    .Op1(multiplexer_6_out), .Op2(multiplexer_7_out), .Sel(controller_1_aluctrl), .Result(ALU_result),
    .Zero(ALU_zero));
  Bit_Extender #(.in_width(32), .out_width(10)) bit_extender_3 (.in(ALU_result), .out(bit_extender_3_out));
  Shifter #(.width(32), .shift("lr")) shifter_2 (.in(ALU_result), .\dist (5'b00010), .out(shifter_2_out));
  and and_1 (and_1_out, controller_1_branch, ALU_zero);
  Shifter #(.width(10), .shift("lr")) shifter_3 (.in(bit_extender_3_out), .\dist (4'b0010), .out(shifter_3_out));
  Bit_Extender #(.in_width(32), .out_width(5)) bit_extender_4 (.in(shifter_2_out), .out(out_7));
  not not_2 (not_2_out, out_6);
  RAM #(.addrWidth(10), .dataWidth(32), .bus("separate")) ram_1 (
    .addr(shifter_3_out), .din(out_8), .data(ram_1_data), .str(out_6), .clk(clock_1_out), .ld(not_2_out),
    .clr(Reset));  // open: sel
  Multiplexer #(.select(2), .width(32)) multiplexer_8 (
    .in0(ALU_result), .in1(ram_1_data), .in2({_31_28, adder_2_out}), .out(out_5), .sel(controller_1_regsrc));  // open: in3, en

  // Other names for the same wires on the sheet: _20_16[4:0] = out_2[20:16]; Instr[31:0] = out_2;
  //   _25_21[4:0] = out_2[25:21]; _5_0[5:0] = out_2[5:0]; _15_0[15:0] = out_2[15:0]; _10_6[4:0] = out_2[10:6];
  //   _15_11[4:0] = out_2[15:11]; _31_26[5:0] = out_2[31:26]; MemAddr[4:0] = out_7; MemData[31:0] = out_8;
  //   MemWrite = out_6; RegAddr[4:0] = out_4; RegData[31:0] = out_5; RegWrite = out_3

  // Notes on the sheet:
  //   contents of rom_1 (hex, n*v repeats v):
  //   34040064 c000c04 c000c0f 8000c1b 34100001 34110004 909021 34080001 34090000 11120004 ad280000
  //   1104021 1314821 8000c09 3e00008 34100001 34110004 34080000 34090000 34020000 11040005 8d320000
  //   521021 1314821 1104021 8000c14 3e00008 3c018765 34324321 3c011234 34335678 253a023
endmodule

module register_file (
  input  WEnable,
  input  clock,
  input  reset,
  input  [4:0] RAddress1,
  input  [4:0] RAddress2,
  input  [4:0] WAddress,
  input  [31:0] WData,
  output [31:0] RData1,
  output [31:0] RData2
);

  wire [31:0] _0, _1, _2, _3, _4, _5, _6, _7, _8, _9, _10, _11, _12, _13, _14, _15, _16, _17, _18, _19, _20,
       _21, _22, _23, _24, _25, _26, _27, _28, _29, _30, _31, decoder_1_out0, multiplexer_1_out,
       multiplexer_3_out, multiplexer_4_out, multiplexer_5_out;

  Decoder #(.select(5), .disabled(0)) decoder_1 (
    .out0(decoder_1_out0[0]), .out1(decoder_1_out0[1]), .out2(decoder_1_out0[2]), .out3(decoder_1_out0[3]),
    .out4(decoder_1_out0[4]), .out5(decoder_1_out0[5]), .out6(decoder_1_out0[6]), .out7(decoder_1_out0[7]),
    .out8(decoder_1_out0[8]), .out9(decoder_1_out0[9]), .out10(decoder_1_out0[10]),
    .out11(decoder_1_out0[11]), .out12(decoder_1_out0[12]), .out13(decoder_1_out0[13]),
    .out14(decoder_1_out0[14]), .out15(decoder_1_out0[15]), .out16(decoder_1_out0[16]),
    .out17(decoder_1_out0[17]), .out18(decoder_1_out0[18]), .out19(decoder_1_out0[19]),
    .out20(decoder_1_out0[20]), .out21(decoder_1_out0[21]), .out22(decoder_1_out0[22]),
    .out23(decoder_1_out0[23]), .out24(decoder_1_out0[24]), .out25(decoder_1_out0[25]),
    .out26(decoder_1_out0[26]), .out27(decoder_1_out0[27]), .out28(decoder_1_out0[28]),
    .out29(decoder_1_out0[29]), .out30(decoder_1_out0[30]), .out31(decoder_1_out0[31]), .sel(WAddress),
    .en(WEnable));
  Register #(.width(32)) register_1 (.D({32{1'b0}}), .en(decoder_1_out0[0]), .Q(_0), .clk(clock), .clr(reset));
  Register #(.width(32)) register_2 (.D(WData), .en(decoder_1_out0[1]), .Q(_1), .clk(clock), .clr(reset));
  Register #(.width(32)) register_3 (.D(WData), .en(decoder_1_out0[2]), .Q(_2), .clk(clock), .clr(reset));
  Register #(.width(32)) register_4 (.D(WData), .en(decoder_1_out0[3]), .Q(_3), .clk(clock), .clr(reset));
  Register #(.width(32)) register_5 (.D(WData), .en(decoder_1_out0[4]), .Q(_4), .clk(clock), .clr(reset));
  Register #(.width(32)) register_6 (.D(WData), .en(decoder_1_out0[5]), .Q(_5), .clk(clock), .clr(reset));
  Register #(.width(32)) register_7 (.D(WData), .en(decoder_1_out0[6]), .Q(_6), .clk(clock), .clr(reset));
  Register #(.width(32)) register_8 (.D(WData), .en(decoder_1_out0[7]), .Q(_7), .clk(clock), .clr(reset));
  Register #(.width(32)) register_9 (.D(WData), .en(decoder_1_out0[8]), .Q(_8), .clk(clock), .clr(reset));
  Register #(.width(32)) register_10 (.D(WData), .en(decoder_1_out0[9]), .Q(_9), .clk(clock), .clr(reset));
  Register #(.width(32)) register_11 (.D(WData), .en(decoder_1_out0[10]), .Q(_10), .clk(clock), .clr(reset));
  Register #(.width(32)) register_12 (.D(WData), .en(decoder_1_out0[11]), .Q(_11), .clk(clock), .clr(reset));
  Register #(.width(32)) register_13 (.D(WData), .en(decoder_1_out0[12]), .Q(_12), .clk(clock), .clr(reset));
  Register #(.width(32)) register_14 (.D(WData), .en(decoder_1_out0[13]), .Q(_13), .clk(clock), .clr(reset));
  Register #(.width(32)) register_15 (.D(WData), .en(decoder_1_out0[14]), .Q(_14), .clk(clock), .clr(reset));
  Register #(.width(32)) register_16 (.D(WData), .en(decoder_1_out0[15]), .Q(_15), .clk(clock), .clr(reset));
  Register #(.width(32)) register_17 (.D(WData), .en(decoder_1_out0[16]), .Q(_16), .clk(clock), .clr(reset));
  Register #(.width(32)) register_18 (.D(WData), .en(decoder_1_out0[17]), .Q(_17), .clk(clock), .clr(reset));
  Register #(.width(32)) register_19 (.D(WData), .en(decoder_1_out0[18]), .Q(_18), .clk(clock), .clr(reset));
  Register #(.width(32)) register_20 (.D(WData), .en(decoder_1_out0[19]), .Q(_19), .clk(clock), .clr(reset));
  Register #(.width(32)) register_21 (.D(WData), .en(decoder_1_out0[20]), .Q(_20), .clk(clock), .clr(reset));
  Register #(.width(32)) register_22 (.D(WData), .en(decoder_1_out0[21]), .Q(_21), .clk(clock), .clr(reset));
  Register #(.width(32)) register_23 (.D(WData), .en(decoder_1_out0[22]), .Q(_22), .clk(clock), .clr(reset));
  Register #(.width(32)) register_24 (.D(WData), .en(decoder_1_out0[23]), .Q(_23), .clk(clock), .clr(reset));
  Register #(.width(32)) register_25 (.D(WData), .en(decoder_1_out0[24]), .Q(_24), .clk(clock), .clr(reset));
  Register #(.width(32)) register_26 (.D(WData), .en(decoder_1_out0[25]), .Q(_25), .clk(clock), .clr(reset));
  Register #(.width(32)) register_27 (.D(WData), .en(decoder_1_out0[26]), .Q(_26), .clk(clock), .clr(reset));
  Register #(.width(32)) register_28 (.D(WData), .en(decoder_1_out0[27]), .Q(_27), .clk(clock), .clr(reset));
  Register #(.width(32)) register_29 (.D(WData), .en(decoder_1_out0[28]), .Q(_28), .clk(clock), .clr(reset));
  Register #(.width(32)) register_30 (.D(WData), .en(decoder_1_out0[29]), .Q(_29), .clk(clock), .clr(reset));
  Register #(.width(32)) register_31 (.D(WData), .en(decoder_1_out0[30]), .Q(_30), .clk(clock), .clr(reset));
  Register #(.width(32)) register_32 (.D(WData), .en(decoder_1_out0[31]), .Q(_31), .clk(clock), .clr(reset));
  Multiplexer #(.select(4), .width(32)) multiplexer_1 (
    .in0(_0), .in1(_1), .in2(_2), .in3(_3), .in4(_4), .in5(_5), .in6(_6), .in7(_7), .in8(_8), .in9(_9),
    .in10(_10), .in11(_11), .in12(_12), .in13(_13), .in14(_14), .in15(_15), .out(multiplexer_1_out),
    .sel(RAddress1[3:0]));  // open: en
  Multiplexer #(.width(32)) multiplexer_2 (
    .in0(multiplexer_1_out), .in1(multiplexer_3_out), .out(RData1), .sel(RAddress1[4]));  // open: en
  Multiplexer #(.select(4), .width(32)) multiplexer_3 (
    .in0(_16), .in1(_17), .in2(_18), .in3(_19), .in4(_20), .in5(_21), .in6(_22), .in7(_23), .in8(_24),
    .in9(_25), .in10(_26), .in11(_27), .in12(_28), .in13(_29), .in14(_30), .in15(_31),
    .out(multiplexer_3_out), .sel(RAddress1[3:0]));  // open: en
  Multiplexer #(.select(4), .width(32)) multiplexer_4 (
    .in0(_0), .in1(_1), .in2(_2), .in3(_3), .in4(_4), .in5(_5), .in6(_6), .in7(_7), .in8(_8), .in9(_9),
    .in10(_10), .in11(_11), .in12(_12), .in13(_13), .in14(_14), .in15(_15), .out(multiplexer_4_out),
    .sel(RAddress2[3:0]));  // open: en
  Multiplexer #(.select(4), .width(32)) multiplexer_5 (
    .in0(_16), .in1(_17), .in2(_18), .in3(_19), .in4(_20), .in5(_21), .in6(_22), .in7(_23), .in8(_24),
    .in9(_25), .in10(_26), .in11(_27), .in12(_28), .in13(_29), .in14(_30), .in15(_31),
    .out(multiplexer_5_out), .sel(RAddress2[3:0]));  // open: en
  Multiplexer #(.width(32)) multiplexer_6 (
    .in0(multiplexer_4_out), .in1(multiplexer_5_out), .out(RData2), .sel(RAddress2[4]));  // open: en

  // Other names for the same wires on the sheet: A1[4:0] = RAddress1; A2[4:0] = RAddress2; WE = WEnable
endmodule

module ALU (
  input  [31:0] Op1,
  input  [31:0] Op2,
  input  [3:0] Sel,
  output [31:0] Result,
  output Zero
);

  wire bitselector_1_out, comparator_1_eq, comparator_1_lt, comparator_2_lt, comparator_3_gt, not_1_out,
       not_3_out;
  wire [4:0] bit_extender_3_out;
  wire [31:0] _0, _1, _2, _3, _4, _5, _6, _7, _8, _9, _10, _11, _12, _13, _14, _15;

  BitSelector #(.width(32)) bitselector_1 (.in(Op1), .out(bitselector_1_out), .sel({5{1'b1}}));
  not not_1 (not_1_out, bitselector_1_out);
  Adder #(.width(32)) adder_1 (.a(Op1), .b(Op2), .out(_2));  // open: cin, cout
  Subtractor #(.width(32)) subtractor_1 (.a(Op1), .b(Op2), .out(_3));  // open: bin, bout
  assign _4 = Op1 & Op2;  // AND_Gate and_1, 32 bits wide
  assign _5 = Op1 | Op2;  // OR_Gate or_1, 32 bits wide
  assign _6 = Op1 ^ Op2;  // XOR_Gate xor_1, 32 bits wide
  assign _1 = {{31{1'b0}}, bitselector_1_out};  // Bit_Extender bit_extender_1
  assign _0 = {{31{1'b0}}, not_1_out};  // Bit_Extender bit_extender_2
  Bit_Extender #(.in_width(32), .out_width(5)) bit_extender_3 (.in(Op1), .out(bit_extender_3_out));
  assign _7 = ~_5;  // NOT_Gate not_2, 32 bits wide
  Comparator #(.width(32)) comparator_1 (.a(Op1), .b(Op2), .eq(comparator_1_eq), .lt(comparator_1_lt));  // open: gt
  Comparator #(.width(32), .mode("unsigned")) comparator_2 (.a(Op1), .b(Op2), .lt(comparator_2_lt));  // open: gt, eq
  Comparator #(.width(32)) comparator_3 (.a(Op1), .b({32{1'b0}}), .gt(comparator_3_gt));  // open: eq, lt
  not not_3 (not_3_out, comparator_3_gt);
  Shifter #(.width(32), .shift("lr")) shifter_1 (.in(Op2), .\dist (bit_extender_3_out), .out(_8));
  Shifter #(.width(32), .shift("ar")) shifter_2 (.in(Op2), .\dist (bit_extender_3_out), .out(_9));
  Shifter #(.width(32)) shifter_3 (.in(Op2), .\dist (bit_extender_3_out), .out(_10));
  assign _11 = {{31{1'b0}}, comparator_1_eq};  // Bit_Extender bit_extender_4
  assign _12 = {{31{1'b0}}, comparator_1_lt};  // Bit_Extender bit_extender_5
  assign _13 = {{31{1'b0}}, comparator_2_lt};  // Bit_Extender bit_extender_6
  assign _14 = {{31{1'b0}}, comparator_3_gt};  // Bit_Extender bit_extender_7
  assign _15 = {{31{1'b0}}, not_3_out};  // Bit_Extender bit_extender_8
  Multiplexer #(.select(4), .width(32)) multiplexer_1 (
    .in0(_0), .in1(_1), .in2(_2), .in3(_3), .in4(_4), .in5(_5), .in6(_6), .in7(_7), .in8(_8), .in9(_9),
    .in10(_10), .in11(_11), .in12(_12), .in13(_13), .in14(_14), .in15(_15), .out(Result), .sel(Sel));  // open: en
  Comparator #(.width(32), .mode("unsigned")) comparator_4 (.a(Result), .b({32{1'b0}}), .eq(Zero));  // open: gt, lt
endmodule

module ALUDecd (
  input  [5:0] OpCode,
  input  [5:0] Funct,
  input  [4:0] RT,
  output [3:0] ALUCtrl
);

  wire nor_1_out;
  wire [3:0] bit_extender_1_out, multiplexer_1_out, multiplexer_2_out, multiplexer_3_out, multiplexer_4_out,
       multiplexer_5_out, multiplexer_6_out, multiplexer_7_out;

  Multiplexer #(.select(3), .width(4)) multiplexer_1 (
    .in0(4'b1010), .in1(4'b0000), .in2(4'b1000), .in3(4'b1001), .in4(4'b1010), .in5(4'b0000), .in6(4'b1000),
    .in7(4'b1001), .out(multiplexer_1_out), .sel(Funct[2:0]));  // open: en
  Multiplexer #(.select(3), .width(4)) multiplexer_2 (
    .in0(4'b0010), .in1(4'b0010), .in2(4'b0011), .in3(4'b0011), .in4(4'b0100), .in5(4'b0101), .in6(4'b0110),
    .in7(4'b0111), .out(multiplexer_2_out), .sel(Funct[2:0]));  // open: en
  Multiplexer #(.select(3), .width(4)) multiplexer_3 (
    .in2(4'b1100), .in3(4'b1101), .out(multiplexer_3_out), .sel(Funct[2:0]));  // open: in0, in1, in4, in5, in6, in7, en
  assign bit_extender_1_out = {{3{1'b0}}, RT[0]};  // Bit_Extender bit_extender_1
  nor nor_1 (nor_1_out, RT[1], RT[2], RT[3], RT[4]);
  Multiplexer #(.width(4)) multiplexer_4 (
    .in1(bit_extender_1_out), .out(multiplexer_4_out), .sel(nor_1_out));  // open: in0, en
  Multiplexer #(.select(3), .width(4)) multiplexer_5 (
    .in0(multiplexer_1_out), .in4(multiplexer_2_out), .in5(multiplexer_3_out), .out(multiplexer_5_out),
    .sel(Funct[5:3]));  // open: in1, in2, in3, in6, in7, en
  Multiplexer #(.select(4), .width(4)) multiplexer_6 (
    .in0(multiplexer_5_out), .in1(multiplexer_4_out), .in2(4'b0000), .in3(4'b0000), .in4(4'b0011),
    .in5(4'b1011), .in6(4'b1110), .in7(4'b1111), .in8(4'b0010), .in9(4'b0010), .in10(4'b1100),
    .in11(4'b1101), .in12(4'b0100), .in13(4'b0101), .in14(4'b0110), .in15(4'b0101), .out(multiplexer_6_out),
    .sel(OpCode[3:0]));  // open: en
  Multiplexer #(.select(4), .width(4)) multiplexer_7 (
    .in3(4'b0010), .in11(4'b0010), .out(multiplexer_7_out), .sel(OpCode[3:0]));  // open: in0, in1, in2, in4, in5, in6, in7, in8, in9, in10, in12, in13, in14, in15, en
  Multiplexer #(.select(2), .width(4)) multiplexer_8 (
    .in0(multiplexer_6_out), .in2(multiplexer_7_out), .out(ALUCtrl), .sel(OpCode[5:4]));  // open: in1, in3, en
endmodule

module ext (
  input  [1:0] ExtOp,
  input  [15:0] Imm,
  output [31:0] Immout
);

  wire [31:0] bit_extender_1_out, bit_extender_2_out, shifter_1_out;

  assign bit_extender_1_out = {{16{Imm[15]}}, Imm};  // Bit_Extender bit_extender_1
  assign bit_extender_2_out = {{16{1'b0}}, Imm};  // Bit_Extender bit_extender_2
  Shifter #(.width(32)) shifter_1 (.in(bit_extender_1_out), .\dist (5'b00010), .out(shifter_1_out));
  Multiplexer #(.select(2), .width(32)) multiplexer_1 (
    .in0(bit_extender_1_out), .in1(bit_extender_2_out), .in2({Imm, {16{1'b0}}}), .in3(shifter_1_out),
    .out(Immout), .sel(ExtOp));  // open: en
endmodule

module Controller (
  input  [5:0] Op,
  input  [5:0] funct,
  input  [4:0] RT,
  input  in_4,
  output jump,
  output [1:0] ExtOp,
  output [1:0] RegSrc,
  output MemWrite,
  output Branch,
  output [3:0] ALUCtrl,
  output [1:0] ALUSrc,
  output [1:0] RegDst,
  output RegWrite
);

  wire add_u, addi_u, \and , andi, beq, bgez, bgtz, blez, bltz, bne, Br, j, jalr, jr, lui, \nor , nor_1_out,
       nor_2_out, nor_3_out, not_7_out, not_14_out, not_15_out, \or , or_2_out, or_8_out, ori, Reg, sll,
       sllv, slt, slti, sltiu, sltu, sra, srav, srl, srlv, sub_u, \xor , xori;
  wire [5:0] and_20_out, bit_extender_1_out;
  wire [10:0] mid, not_11_out;

  not not_1 (mid[10], Op[5]);
  not not_2 (mid[8], Op[4]);
  not not_3 (mid[2], Op[1]);
  not not_4 (mid[6], Op[3]);
  not not_5 (mid[4], Op[2]);
  not not_6 (mid[0], Op[0]);
  and and_1 (addi_u, mid[2], mid[4], Op[3], mid[8], mid[10]);
  and and_2 (slti, mid[0], Op[1], mid[4], Op[3], mid[8], mid[10]);
  and and_3 (andi, mid[0], mid[2], Op[2], Op[3], mid[8], mid[10]);
  and and_4 (xori, mid[0], Op[1], Op[2], Op[3], mid[8], mid[10]);
  and and_5 (j, mid[0], Op[1], mid[4], mid[6], mid[8], mid[10]);
  and and_6 (sltiu, Op[0], Op[1], mid[4], Op[3], mid[8], mid[10]);
  and and_7 (ori, Op[0], mid[2], Op[2], Op[3], mid[8], mid[10]);
  and and_8 (lui, Op[0], Op[1], Op[2], Op[3], mid[8], mid[10]);
  and and_9 (RegDst[1], Op[0], Op[1], mid[4], mid[6], mid[8], mid[10]);
  not not_7 (not_7_out, RT[0]);
  nor nor_1 (nor_1_out, RT[0], RT[1], RT[2], RT[3], RT[4]);
  nor nor_2 (nor_2_out, not_7_out, RT[1], RT[2], RT[3], RT[4]);
  and and_10 (bltz, nor_1_out, Br);
  and and_11 (beq, mid[0], mid[2], Op[2], mid[6], mid[8], mid[10]);
  and and_12 (blez, mid[0], Op[1], Op[2], mid[6], mid[8], mid[10]);
  and and_13 (RegSrc[0], Op[0], Op[1], mid[4], mid[6], mid[8], Op[5]);
  and and_14 (Reg, mid[0], mid[2], mid[4], mid[6], mid[8], mid[10]);
  and and_15 (bgez, Br, nor_2_out);
  and and_16 (bne, Op[0], mid[2], Op[2], mid[6], mid[8], mid[10]);
  and and_17 (bgtz, Op[0], Op[1], Op[2], mid[6], mid[8], mid[10]);
  and and_18 (MemWrite, Op[0], Op[1], mid[4], Op[3], mid[8], Op[5]);
  and and_19 (Br, Op[0], mid[2], mid[4], mid[6], mid[8], mid[10]);
  assign bit_extender_1_out = {{5{Reg}}, Reg};  // Bit_Extender bit_extender_1
  not not_8 (not_11_out[10], and_20_out[5]);
  not not_9 (not_11_out[8], and_20_out[4]);
  assign and_20_out = bit_extender_1_out & funct;  // AND_Gate and_20, 6 bits wide
  not not_10 (not_11_out[2], and_20_out[1]);
  not not_11 (not_11_out[0], and_20_out[0]);
  not not_12 (not_11_out[6], and_20_out[3]);
  not not_13 (not_11_out[4], and_20_out[2]);
  not not_14 (not_14_out, in_4);
  and and_21 (sllv, not_11_out[0], not_11_out[2], and_20_out[2], not_11_out[6], not_11_out[8], not_11_out[10]);
  and and_22 (srlv, not_11_out[0], and_20_out[1], and_20_out[2], not_11_out[6], not_11_out[8], not_11_out[10]);
  and and_23 (add_u, not_11_out[2], not_11_out[4], not_11_out[6], not_11_out[8], and_20_out[5]);
  and and_24 (sub_u, and_20_out[1], not_11_out[4], not_11_out[6], not_11_out[8], and_20_out[5]);
  and and_25 (\and , not_11_out[0], not_11_out[2], and_20_out[2], not_11_out[6], not_11_out[8], and_20_out[5]);
  and and_26 (\xor , not_11_out[0], and_20_out[1], and_20_out[2], not_11_out[6], not_11_out[8], and_20_out[5]);
  and and_27 (slt, not_11_out[0], and_20_out[1], not_11_out[4], and_20_out[3], not_11_out[8], and_20_out[5]);
  and and_28 (jr, not_11_out[0], not_11_out[2], not_11_out[4], and_20_out[3], not_11_out[8], not_11_out[10]);
  and and_29 (srl, not_11_out[0], and_20_out[1], not_11_out[4], not_11_out[6], not_11_out[8], not_11_out[10]);
  and and_30 (sll, not_11_out[0], not_11_out[2], not_11_out[4], not_14_out, not_11_out[6], not_11_out[8], not_11_out[10]);
  and and_31 (srav, and_20_out[0], and_20_out[1], and_20_out[2], not_11_out[6], not_11_out[8], not_11_out[10]);
  and and_32 (\or , and_20_out[0], not_11_out[2], and_20_out[2], not_11_out[6], not_11_out[8], and_20_out[5]);
  and and_33 (\nor , and_20_out[0], and_20_out[1], and_20_out[2], not_11_out[6], not_11_out[8], and_20_out[5]);
  and and_34 (sltu, and_20_out[0], and_20_out[1], not_11_out[4], and_20_out[3], not_11_out[8], and_20_out[5]);
  and and_35 (jalr, and_20_out[0], not_11_out[2], not_11_out[4], and_20_out[3], not_11_out[8], not_11_out[10]);
  and and_36 (sra, and_20_out[0], and_20_out[1], not_11_out[4], not_11_out[6], not_11_out[8], not_11_out[10]);
  or or_1 (ExtOp[0], sltiu, andi, Branch, ori, xori);
  or or_2 (or_2_out, RegSrc[0], RegDst[1], ALUSrc[0], jalr, Reg);
  nor nor_3 (nor_3_out, in_4, j, MemWrite);
  or or_3 (jump, jr, j, RegDst[1], jalr);
  or or_4 (ExtOp[1], lui, Branch);
  or or_5 (RegSrc[1], jalr, RegDst[1]);
  or or_6 (Branch, beq, bne, blez, bgtz, Br);
  ALUDecd aludecd_1 (.OpCode(Op), .Funct(funct), .RT(RT), .ALUCtrl(ALUCtrl));
  or or_7 (ALUSrc[0], RegDst[1], RegSrc[0], addi_u, slti, sltiu, andi, ori, xori, lui, MemWrite, j);
  or or_8 (or_8_out, sll, srl, sra);
  and and_37 (RegDst[0], Reg, not_15_out);
  not not_15 (not_15_out, in_4);
  and and_38 (RegWrite, or_2_out, nor_3_out);
  and and_39 (ALUSrc[1], or_8_out, Reg);

  // Other names for the same wires on the sheet: mid (some bits) = Op; isImm = ALUSrc[0]; nop = in_4; jal = RegDst[1];
  //   lw = RegSrc[0]; sw = MemWrite
endmodule

module test (
  output [31:0] out_1,
  output out_2,
  output [4:0] out_3,
  output [31:0] out_4,
  output out_5,
  output [4:0] out_6,
  output [31:0] out_7
);

  wire comparator_1_gt;
  wire [7:0] counter_1_q;

  Counter counter_1 (.Q(counter_1_q));  // open: load, D, count, carry, clk, clr
  Comparator comparator_1 (.a(8'h4), .b(counter_1_q), .gt(comparator_1_gt));  // open: eq, lt
  main main_1 (
    .Reset(comparator_1_gt), .out_2(out_1), .out_3(out_2), .out_4(out_3), .out_5(out_4), .out_6(out_5),
    .out_7(out_6), .out_8(out_7));
endmodule

module ALUwithOver (
  input  [31:0] Op1,
  input  [31:0] Op2,
  input  [3:0] Sel,
  output [31:0] Result,
  output Zero,
  output Overflow
);

  wire _01, _02, _03, bitselector_4_out, bitselector_5_out, comparator_1_eq, comparator_1_lt,
       comparator_2_lt, comparator_3_gt, multiplexer_1_out, multiplexer_2_out, multiplexer_3_out, not_1_out,
       not_3_out, xor_2_out, xor_3_out, xor_4_out;
  wire [4:0] bit_extender_3_out;
  wire [31:0] _0, _1, _2, _3, _4, _5, _6, _7, _8, _9, _10, _11, _12, _13, _14, _15;

  BitSelector #(.width(32)) bitselector_1 (.in(Op1), .out(_01), .sel({5{1'b1}}));
  not not_1 (not_1_out, _01);
  Adder #(.width(32)) adder_1 (.a(Op1), .b(Op2), .out(_2));  // open: cin, cout
  BitSelector #(.width(32)) bitselector_2 (.in(_2), .out(_02), .sel({5{1'b1}}));
  Subtractor #(.width(32)) subtractor_1 (.a(Op1), .b(Op2), .out(_3));  // open: bin, bout
  BitSelector #(.width(32)) bitselector_3 (.in(_3), .out(_03), .sel({5{1'b1}}));
  assign _4 = Op1 & Op2;  // AND_Gate and_1, 32 bits wide
  assign _5 = Op1 | Op2;  // OR_Gate or_1, 32 bits wide
  assign _6 = Op1 ^ Op2;  // XOR_Gate xor_1, 32 bits wide
  assign _1 = {{31{1'b0}}, _01};  // Bit_Extender bit_extender_1
  assign _0 = {{31{1'b0}}, not_1_out};  // Bit_Extender bit_extender_2
  Bit_Extender #(.in_width(32), .out_width(5)) bit_extender_3 (.in(Op2), .out(bit_extender_3_out));
  assign _7 = ~_5;  // NOT_Gate not_2, 32 bits wide
  BitSelector #(.width(32)) bitselector_4 (.in(Op1), .out(bitselector_4_out), .sel({5{1'b1}}));
  BitSelector #(.width(32)) bitselector_5 (.in(Op2), .out(bitselector_5_out), .sel({5{1'b1}}));
  Comparator #(.width(32)) comparator_1 (.a(Op1), .b(Op2), .eq(comparator_1_eq), .lt(comparator_1_lt));  // open: gt
  Comparator #(.width(32), .mode("unsigned")) comparator_2 (.a(Op1), .b(Op2), .lt(comparator_2_lt));  // open: gt, eq
  Comparator #(.width(32)) comparator_3 (.a(Op1), .b({32{1'b0}}), .gt(comparator_3_gt));  // open: eq, lt
  not not_3 (not_3_out, comparator_3_gt);
  Shifter #(.width(32), .shift("lr")) shifter_1 (.in(Op1), .\dist (bit_extender_3_out), .out(_8));
  Shifter #(.width(32), .shift("ar")) shifter_2 (.in(Op1), .\dist (bit_extender_3_out), .out(_9));
  Shifter #(.width(32)) shifter_3 (.in(Op1), .\dist (bit_extender_3_out), .out(_10));
  xor xor_2 (xor_2_out, _01, _02);
  Multiplexer multiplexer_1 (.in0(xor_2_out), .in1(1'b0), .out(multiplexer_1_out), .sel(xor_3_out));  // open: en
  xor xor_3 (xor_3_out, bitselector_4_out, bitselector_5_out);
  Multiplexer multiplexer_2 (.in0(1'b0), .in1(xor_4_out), .out(multiplexer_2_out), .sel(xor_3_out));  // open: en
  xor xor_4 (xor_4_out, _01, _03);
  assign _11 = {{31{1'b0}}, comparator_1_eq};  // Bit_Extender bit_extender_4
  assign _12 = {{31{1'b0}}, comparator_1_lt};  // Bit_Extender bit_extender_5
  assign _13 = {{31{1'b0}}, comparator_2_lt};  // Bit_Extender bit_extender_6
  assign _14 = {{31{1'b0}}, comparator_3_gt};  // Bit_Extender bit_extender_7
  assign _15 = {{31{1'b0}}, not_3_out};  // Bit_Extender bit_extender_8
  Multiplexer #(.select(2)) multiplexer_3 (
    .in0(1'b0), .in1(1'b0), .in2(multiplexer_1_out), .in3(multiplexer_2_out), .out(multiplexer_3_out),
    .sel(Sel[1:0]));  // open: en
  Multiplexer #(.select(2)) multiplexer_4 (
    .in0(multiplexer_3_out), .in1(1'b0), .in2(1'b0), .in3(1'b0), .out(Overflow), .sel(Sel[3:2]));  // open: en
  Multiplexer #(.select(4), .width(32)) multiplexer_5 (
    .in0(_0), .in1(_1), .in2(_2), .in3(_3), .in4(_4), .in5(_5), .in6(_6), .in7(_7), .in8(_8), .in9(_9),
    .in10(_10), .in11(_11), .in12(_12), .in13(_13), .in14(_14), .in15(_15), .out(Result), .sel(Sel));  // open: en
  Comparator #(.width(32), .mode("unsigned")) comparator_4 (.a(Result), .b({32{1'b0}}), .eq(Zero));  // open: gt, lt
endmodule
